// Logisim project proyecto1_arqui_2024.circ as structural Verilog: 1 circuit, main circuit main
module main (
  input  A,
  input  B,
  input  C,
  input  D,
  input  E,
  output out_6
);

  wire and_1_out, and_2_out, and_3_out, and_4_out, decoder_1_out0, decoder_1_out2, decoder_1_out4,
       decoder_1_out7, decoder_1_out11, decoder_1_out12, decoder_1_out13, decoder_1_out15, decoder_1_out20,
       not_1_out, not_2_out, not_3_out, or_2_out;
  wire [1:0] undriven;

  not not_1 (not_1_out, D);
  not not_2 (not_2_out, E);
  not not_3 (not_3_out, B);
  Decoder #(.enable("false"), .select(5)) decoder_1 (
    .out0(decoder_1_out0), .out2(decoder_1_out2), .out4(decoder_1_out4), .out7(decoder_1_out7),
    .out11(decoder_1_out11), .out12(decoder_1_out12), .out13(decoder_1_out13), .out15(decoder_1_out15),
    .out20(decoder_1_out20), .sel({A, {2{B}}, D, E}));  // open: out1, out3, out5, out6, out8, out9, out10, out14, out16, out17, out18, out19, out21, out22, out23, out24, out25, out26, out27, out28, out29, out30, out31
  and and_1 (and_1_out, not_3_out, E);
  and and_2 (and_2_out, not_3_out, not_1_out);
  and and_3 (and_3_out, D, E);
  and and_4 (and_4_out, not_1_out, not_2_out);
  LED led_1 (.in(out_6));
  or or_1 (out_6, decoder_1_out0, decoder_1_out2, decoder_1_out4, decoder_1_out7, decoder_1_out11, decoder_1_out12, decoder_1_out13, decoder_1_out15, decoder_1_out20);
  or or_2 (or_2_out, and_1_out, and_2_out, and_4_out);
  Multiplexer #(.select(2)) multiplexer_1 (
    .in0(and_3_out), .in1(B), .in2(or_2_out), .in3(and_4_out), .sel(undriven));  // open: out

  assign C = B;

  // Notes on the sheet:
  //   B'E
  //   B'D'
  //   DE
  //   D'E'
endmodule
